// Logisim project GuitarTranscriptionProject.circ as structural Verilog: 1 circuit, main circuit main
module main (
  input  S6,
  input  S5,
  input  S4,
  input  S3,
  input  S2,
  input  S1,
  input  S6_2,
  input  S5_2,
  input  S4_2,
  input  S3_2,
  input  S2_2,
  input  S1_2,
  input  S6_3,
  input  S5_3,
  input  S4_3,
  input  S3_3,
  input  S2_3,
  input  S1_3,
  input  S6_4,
  input  S5_4,
  input  S4_4,
  input  S3_4,
  input  S2_4,
  input  S1_4,
  input  S6_5,
  input  S5_5,
  input  S4_5,
  input  S3_5,
  input  S2_5,
  input  S1_5,
  output [5:0] Fret_1_Output,
  output [5:0] Fret_2_Output,
  output [5:0] Fret_3_Output,
  output [5:0] Fret_4_Output,
  output [5:0] Fret_24_Output
);


  assign Fret_1_Output = {S6, S5, S4, S3, S2, S1};
  assign Fret_2_Output = {S6_2, S5_2, S4_2, S3_2, S2_2, S1_2};
  assign Fret_3_Output = {S6_3, S5_3, S4_3, S3_3, S2_3, S1_3};
  assign Fret_4_Output = {S6_4, S5_4, S4_4, S3_4, S2_4, S1_4};
  assign Fret_24_Output = {S6_5, S5_5, S4_5, S3_5, S2_5, S1_5};

  // Notes on the sheet:
  //   Fret 1 Input
  //   Fret 2 Input
  //   Fret 3 Input
  //   Fret 4 Input
  //   Fret 24 Input
  //   Open G Chord
  //   .... etc ...
  //   Store everything in a 24x6 Matrix
endmodule
